# Fritzing sketch montagem_portao (saved by Fritzing 0.9.3b)
circuit board: 8.46667cm x 5.64444cm
breadboards: 1

parts:
  hc-sr1 = hc-sr04
  Componente1 = Arduino Uno (Rev3)
  IC1 = L293D [package=THT]
  S1 = Momentary Switch [package=ksa_sealed_tac_switch]
  R1 = Resistor [tolerance=±5% resistance=10k package=THT]
  M1 = DC Motor
  VCC1 = Battery block 9V

nets:
  N1: hc-sr1.VCC, IC1.+V, S1.2
  N2: hc-sr1.Trig, Componente1.D9_PWM
  N3: hc-sr1.Echo, Componente1.D10_PWM/SS
  N4: hc-sr1.GND, IC1.0V, R1.Pin_1, VCC1.-
  N5: Componente1.D11_PWM/MOSI, S1.3
  N6: Componente1.D3_PWM, IC1.Enable_2
  N7: Componente1.D4, IC1.In_4
  N8: Componente1.D5_PWM, IC1.In_3
  N9: IC1.+Vmotor, VCC1.+
  N10: IC1.Out_3_(_Controlled_by_Enable_2_), M1.pin_2
  N11: IC1.Out_4_(_Controlled_by_Enable_2_), M1.pin_1
  N12: S1.4, R1.Pin_0
